# Fritzing sketch NodeMCU-5V-analog (saved by Fritzing 0.9.3b)
breadboards: 1

parts:
  U1 = LM 358 Dual Op-Amp [package="DIP8 [THT]"]
  U2 = NodeMCU V3.0
  D1 = Diode [package=diode-1n4148]
  D2 = Diode [package=diode-1n4148]
  R1b = Resistor [tolerance=±5% resistance=220k package=THT]
  R1a = Resistor [tolerance=±5% resistance=47k package=THT]
  R2 = Resistor [tolerance=±5% resistance=470k package=THT]
  R3 = Resistor [tolerance=±5% resistance=100 package=THT]
  D3 = Diode [package=diode-1n4148]

nets:
  N1: U1.connector0, U1.connector1, R3.Pin_1
  N2: U1.connector2, D1.A, D2.C, R1b.Pin_1, R2.Pin_0
  N3: U1.connector3, U2.GND#6, U2.GND#13, U2.GND#16, U2.GND#33, D2.A, R2.Pin_1
  N4: U1.connector7, U2.VU, R1a.Pin_0
  N5: U2.3V3, D1.C, D3.C
  N6: U2.A0, R3.Pin_0, D3.A
  N7: R1b.Pin_0, R1a.Pin_1

notes:
  Barramento Superior - 5Vusb
  Barramento inferior - 3v3 da NodeMCU

custom parts:
  NodeMCU V3.0: ESP8266 based NodeMCU
